// Logisim project Arethmitics.circ as structural Verilog
// H-A
module Half_Adder_1bit (
  input  A,
  input  B,
  output S,
  output Co
);

  xor xor_1 (S, A, B);
  and and_1 (Co, B, A);
endmodule

// F-A.1
module Full_Adder_1bit (
  input  A,
  input  B,
  input  Ci,
  output S,
  output Co
);

  wire half_adder_1bit_1_co, half_adder_1bit_1_s, half_adder_1bit_2_co;

  Half_Adder_1bit half_adder_1bit_1 (.A(A), .B(B), .S(half_adder_1bit_1_s), .Co(half_adder_1bit_1_co));
  Half_Adder_1bit half_adder_1bit_2 (.A(half_adder_1bit_1_s), .B(Ci), .S(S), .Co(half_adder_1bit_2_co));
  or or_1 (Co, half_adder_1bit_2_co, half_adder_1bit_1_co);

  // Notes on the sheet:
  //   A ⨁ B
  //   AB
  //   (A ⨁ B) ⨁ Ci
  //   (A ⨁ B)Ci
endmodule

// F-A.4
module Full_Adder_4bit (
  input  A3,
  input  A2,
  input  A1,
  input  A0,
  input  Ci,
  input  B3,
  input  B2,
  input  B1,
  input  B0,
  output Co,
  output S3,
  output S2,
  output S1,
  output S0
);

  wire full_adder_1bit_1_co, full_adder_1bit_3_co, full_adder_1bit_4_co;

  Full_Adder_1bit full_adder_1bit_1 (.A(A2), .B(B2), .Ci(full_adder_1bit_3_co), .S(S2), .Co(full_adder_1bit_1_co));
  Full_Adder_1bit full_adder_1bit_2 (.A(A3), .B(B3), .Ci(full_adder_1bit_1_co), .S(S3), .Co(Co));
  Full_Adder_1bit full_adder_1bit_3 (.A(A1), .B(B1), .Ci(full_adder_1bit_4_co), .S(S1), .Co(full_adder_1bit_3_co));
  Full_Adder_1bit full_adder_1bit_4 (.A(A0), .B(B0), .Ci(Ci), .S(S0), .Co(full_adder_1bit_4_co));
endmodule

// H-S
module Half_Subtractor_1bit (
  input  A,
  input  B,
  output D,
  output Bo
);

  wire not_1_out;

  xor xor_1 (D, A, B);
  and and_1 (Bo, B, not_1_out);
  not not_1 (not_1_out, A);
endmodule

// F-S.1
module Full_Subtractor_1bit (
  input  A,
  input  B,
  input  Bi,
  output D,
  output Bo
);

  wire half_subtractor_1bit_1_bo, half_subtractor_1bit_1_d, half_subtractor_1bit_2_bo;

  Half_Subtractor_1bit half_subtractor_1bit_1 (
    .A(A), .B(B), .D(half_subtractor_1bit_1_d), .Bo(half_subtractor_1bit_1_bo));
  Half_Subtractor_1bit half_subtractor_1bit_2 (
    .A(half_subtractor_1bit_1_d), .B(Bi), .D(D), .Bo(half_subtractor_1bit_2_bo));
  or or_1 (Bo, half_subtractor_1bit_2_bo, half_subtractor_1bit_1_bo);

  // Notes on the sheet:
  //   A ⨁ B
  //   ĀB
  //   (A ⨁ B) ⨁ Bi
  //   (A ⨁ B)'Bi
endmodule

// F-S.4
module Full_Subtractor_4bit (
  input  A3,
  input  A2,
  input  A1,
  input  A0,
  input  Bi,
  input  B3,
  input  B2,
  input  B1,
  input  B0,
  output Bo,
  output D3,
  output D2,
  output D1,
  output D0
);

  wire full_subtractor_1bit_1_bo, full_subtractor_1bit_3_bo, full_subtractor_1bit_4_bo;

  Full_Subtractor_1bit full_subtractor_1bit_1 (
    .A(A2), .B(B2), .Bi(full_subtractor_1bit_3_bo), .D(D2), .Bo(full_subtractor_1bit_1_bo));
  Full_Subtractor_1bit full_subtractor_1bit_2 (.A(A3), .B(B3), .Bi(full_subtractor_1bit_1_bo), .D(D3), .Bo(Bo));
  Full_Subtractor_1bit full_subtractor_1bit_3 (
    .A(A1), .B(B1), .Bi(full_subtractor_1bit_4_bo), .D(D1), .Bo(full_subtractor_1bit_3_bo));
  Full_Subtractor_1bit full_subtractor_1bit_4 (.A(A0), .B(B0), .Bi(Bi), .D(D0), .Bo(full_subtractor_1bit_4_bo));
endmodule

// F-AS.4
module Full_Adder_Subtractor_4bit (
  input  A3,
  input  A2,
  input  A1,
  input  A0,
  input  M,
  input  B3,
  input  B2,
  input  B1,
  input  B0,
  output Xo,
  output O3,
  output O2,
  output O1,
  output O0
);

  wire full_adder_1bit_2_co, full_adder_1bit_3_co, full_adder_1bit_4_co, xor_1_out, xor_2_out, xor_3_out,
       xor_4_out;

  Full_Adder_1bit full_adder_1bit_1 (.A(A3), .B(xor_1_out), .Ci(full_adder_1bit_2_co), .S(O3), .Co(Xo));
  Full_Adder_1bit full_adder_1bit_2 (
    .A(A2), .B(xor_2_out), .Ci(full_adder_1bit_3_co), .S(O2), .Co(full_adder_1bit_2_co));
  xor xor_1 (xor_1_out, B3, M);
  Full_Adder_1bit full_adder_1bit_3 (
    .A(A1), .B(xor_3_out), .Ci(full_adder_1bit_4_co), .S(O1), .Co(full_adder_1bit_3_co));
  xor xor_2 (xor_2_out, B2, M);
  xor xor_3 (xor_3_out, B1, M);
  Full_Adder_1bit full_adder_1bit_4 (.A(A0), .B(xor_4_out), .Ci(M), .S(O0), .Co(full_adder_1bit_4_co));
  xor xor_4 (xor_4_out, B0, M);
endmodule

// Mlt.2
module Multiplier_2x2 (
  input  A0,
  input  A1,
  input  B0,
  input  B1,
  output C0,
  output C1,
  output C2,
  output C3
);

  wire A0B1_out, A1B0_out, half_adder_1bit_1_co;

  and A0B0 (C0, A0, B0);
  and A0B1 (A0B1_out, A0, B1);
  and A1B0 (A1B0_out, A1, B0);
  // AND_Gate A1B1 has open pins: in1=A1, in3=B1, out=open
  Half_Adder_1bit half_adder_1bit_1 (.A(A0B1_out), .B(A1B0_out), .S(C1), .Co(half_adder_1bit_1_co));
endmodule
