// Logisim project Arethmitics2.circ as structural Verilog
// H-A
module Half_Adder_1bit (
  input  A,
  input  B,
  output S,
  output Co
);

  xor xor_1 (S, A, B);
  and and_1 (Co, B, A);
endmodule

// F-A.1
module Full_Adder_1bit (
  input  A,
  input  B,
  input  Ci,
  output S,
  output Co
);

  wire half_adder_1bit_1_co, half_adder_1bit_1_s, half_adder_1bit_2_co;

  Half_Adder_1bit half_adder_1bit_1 (.A(A), .B(B), .S(half_adder_1bit_1_s), .Co(half_adder_1bit_1_co));
  Half_Adder_1bit half_adder_1bit_2 (.A(half_adder_1bit_1_s), .B(Ci), .S(S), .Co(half_adder_1bit_2_co));
  or or_1 (Co, half_adder_1bit_2_co, half_adder_1bit_1_co);

  // Notes on the sheet:
  //   A ⨁ B
  //   AB
  //   (A ⨁ B) ⨁ Ci
  //   (A ⨁ B)Ci
endmodule

// F-A.4
module Full_Adder_4bit (
  input  A3,
  input  A2,
  input  A1,
  input  A0,
  input  Ci,
  input  B3,
  input  B2,
  input  B1,
  input  B0,
  output Co,
  output S3,
  output S2,
  output S1,
  output S0
);

  wire full_adder_1bit_1_co, full_adder_1bit_3_co, full_adder_1bit_4_co;

  Full_Adder_1bit full_adder_1bit_1 (.A(A2), .B(B2), .Ci(full_adder_1bit_3_co), .S(S2), .Co(full_adder_1bit_1_co));
  Full_Adder_1bit full_adder_1bit_2 (.A(A3), .B(B3), .Ci(full_adder_1bit_1_co), .S(S3), .Co(Co));
  Full_Adder_1bit full_adder_1bit_3 (.A(A1), .B(B1), .Ci(full_adder_1bit_4_co), .S(S1), .Co(full_adder_1bit_3_co));
  Full_Adder_1bit full_adder_1bit_4 (.A(A0), .B(B0), .Ci(Ci), .S(S0), .Co(full_adder_1bit_4_co));
endmodule

// H-S
module Half_Subtractor_1bit (
  input  A,
  input  B,
  output D,
  output Bo
);

  wire not_1_out;

  xor xor_1 (D, A, B);
  and and_1 (Bo, B, not_1_out);
  not not_1 (not_1_out, A);
endmodule

// F-S.1
module Full_Subtractor_1bit (
  input  A,
  input  B,
  input  Bi,
  output D,
  output Bo
);

  wire half_subtractor_1bit_1_bo, half_subtractor_1bit_1_d, half_subtractor_1bit_2_bo;

  Half_Subtractor_1bit half_subtractor_1bit_1 (
    .A(A), .B(B), .D(half_subtractor_1bit_1_d), .Bo(half_subtractor_1bit_1_bo));
  Half_Subtractor_1bit half_subtractor_1bit_2 (
    .A(half_subtractor_1bit_1_d), .B(Bi), .D(D), .Bo(half_subtractor_1bit_2_bo));
  or or_1 (Bo, half_subtractor_1bit_2_bo, half_subtractor_1bit_1_bo);

  // Notes on the sheet:
  //   A ⨁ B
  //   ĀB
  //   (A ⨁ B) ⨁ Bi
  //   (A ⨁ B)'Bi
endmodule

// F-S.4
module Full_Subtractor_4bit (
  input  A3,
  input  A2,
  input  A1,
  input  A0,
  input  Bi,
  input  B3,
  input  B2,
  input  B1,
  input  B0,
  output Bo,
  output D3,
  output D2,
  output D1,
  output D0
);

  wire full_subtractor_1bit_2_bo, full_subtractor_1bit_3_bo, full_subtractor_1bit_4_bo;

  Full_Subtractor_1bit full_subtractor_1bit_1 (.A(A3), .B(B3), .Bi(full_subtractor_1bit_2_bo), .D(D3), .Bo(Bo));
  Full_Subtractor_1bit full_subtractor_1bit_2 (
    .A(A2), .B(B2), .Bi(full_subtractor_1bit_3_bo), .D(D2), .Bo(full_subtractor_1bit_2_bo));
  Full_Subtractor_1bit full_subtractor_1bit_3 (
    .A(A1), .B(B1), .Bi(full_subtractor_1bit_4_bo), .D(D1), .Bo(full_subtractor_1bit_3_bo));
  Full_Subtractor_1bit full_subtractor_1bit_4 (.A(A0), .B(B0), .Bi(Bi), .D(D0), .Bo(full_subtractor_1bit_4_bo));
endmodule

// F-AS.4
module Full_Adder_Subtractor_4bit (
  input  A3,
  input  A2,
  input  A1,
  input  A0,
  input  M,
  input  B3,
  input  B2,
  input  B1,
  input  B0,
  output Xo,
  output O3,
  output O2,
  output O1,
  output O0
);

  wire full_adder_1bit_2_co, full_adder_1bit_3_co, full_adder_1bit_4_co, xor_1_out, xor_2_out, xor_3_out,
       xor_4_out;

  Full_Adder_1bit full_adder_1bit_1 (.A(A3), .B(xor_1_out), .Ci(full_adder_1bit_2_co), .S(O3), .Co(Xo));
  Full_Adder_1bit full_adder_1bit_2 (
    .A(A2), .B(xor_2_out), .Ci(full_adder_1bit_3_co), .S(O2), .Co(full_adder_1bit_2_co));
  xor xor_1 (xor_1_out, B3, M);
  Full_Adder_1bit full_adder_1bit_3 (
    .A(A1), .B(xor_3_out), .Ci(full_adder_1bit_4_co), .S(O1), .Co(full_adder_1bit_3_co));
  xor xor_2 (xor_2_out, B2, M);
  xor xor_3 (xor_3_out, B1, M);
  Full_Adder_1bit full_adder_1bit_4 (.A(A0), .B(xor_4_out), .Ci(M), .S(O0), .Co(full_adder_1bit_4_co));
  xor xor_4 (xor_4_out, B0, M);
endmodule

// Mlt.2x2
module Multiplier_2x2_bit (
  input  A0,
  input  A1,
  input  B0,
  input  B1,
  output C0,
  output C1,
  output C2,
  output C3
);

  wire A0B1_out, A1B0_out, A1B1_out, half_adder_1bit_1_co;

  and A0B0 (C0, A0, B0);
  and A0B1 (A0B1_out, A0, B1);
  and A1B0 (A1B0_out, A1, B0);
  and A1B1 (A1B1_out, A1, B1);
  Half_Adder_1bit half_adder_1bit_1 (.A(A0B1_out), .B(A1B0_out), .S(C1), .Co(half_adder_1bit_1_co));
  Half_Adder_1bit half_adder_1bit_2 (.A(half_adder_1bit_1_co), .B(A1B1_out), .S(C2), .Co(C3));
endmodule

// Mlt.2x4
module Multiplier_2x4_bit (
  input  A0,
  input  B0,
  input  B1,
  input  B2,
  input  B3,
  input  A1,
  output C0,
  output C1,
  output C2,
  output C3,
  output C4,
  output C5
);

  wire A0B1_out, A0B2_out, A0B3_out, A1B0_out, A1B1_out, A1B2_out, A1B3_out;

  and A1B3 (A1B3_out, A1, B3);
  and A0B1 (A0B1_out, A0, B1);
  and A0B3 (A0B3_out, A0, B3);
  and A0B2 (A0B2_out, A0, B2);
  Full_Adder_4bit full_adder_4bit_1 (
    .Ci(1'b0), .A3(1'b0), .A2(A0B3_out), .A1(A0B2_out), .A0(A0B1_out), .Co(C5), .S3(C4), .B3(A1B3_out),
    .S2(C3), .B2(A1B2_out), .S1(C2), .B1(A1B1_out), .S0(C1), .B0(A1B0_out));
  and A1B0 (A1B0_out, A1, B0);
  and A1B1 (A1B1_out, A1, B1);
  and A1B2 (A1B2_out, A1, B2);
  and A0B0 (C0, A0, B0);
endmodule

// Cmp.1
module Comperator_1bit (
  input  A,
  input  B,
  output B_A,
  output A_B,
  output A_B_2
);

  wire not_1_out, not_2_out;

  not not_1 (not_1_out, A);
  not not_2 (not_2_out, B);
  and A_prime_B (B_A, not_1_out, B);
  and AB_prime (A_B_2, A, not_2_out);
  nor nor_1 (A_B, B_A, A_B_2);
endmodule

// Cmp.2
module Comperator_2bit (
  input  A1,
  input  B1,
  input  A0,
  input  B0,
  output A_B,
  output A_B_2,
  output A_B_3
);

  wire and_1_out, and_3_out, comperator_1bit_1_a_b, comperator_1bit_1_a_b_2, comperator_1bit_1_b_a,
       comperator_1bit_2_a_b, comperator_1bit_2_a_b_2, comperator_1bit_2_b_a;

  Comperator_1bit comperator_1bit_1 (
    .A(A1), .B(B1), .B_A(comperator_1bit_1_b_a), .A_B(comperator_1bit_1_a_b), .A_B_2(comperator_1bit_1_a_b_2));
  Comperator_1bit comperator_1bit_2 (
    .A(A0), .B(B0), .B_A(comperator_1bit_2_b_a), .A_B(comperator_1bit_2_a_b), .A_B_2(comperator_1bit_2_a_b_2));
  or or_1 (A_B, comperator_1bit_1_b_a, and_1_out);
  and and_1 (and_1_out, comperator_1bit_1_a_b, comperator_1bit_2_b_a);
  and and_2 (A_B_2, comperator_1bit_1_a_b, comperator_1bit_2_a_b);
  or or_2 (A_B_3, comperator_1bit_1_a_b_2, and_3_out);
  and and_3 (and_3_out, comperator_1bit_1_a_b, comperator_1bit_2_a_b_2);
endmodule

// Dcdr 3->8
module Decoder_3__8 (
  input  E,
  input  X0,
  input  X1,
  input  X2,
  output y0,
  output y1,
  output y2,
  output y3,
  output y4,
  output y5,
  output y6,
  output y7
);

  wire not_1_out, not_2_out, not_3_out;

  not not_1 (not_1_out, X0);
  not not_2 (not_2_out, X1);
  not not_3 (not_3_out, X2);
  and and_1 (y0, not_1_out, not_2_out, not_3_out, E);
  and and_2 (y1, not_1_out, not_2_out, X2, E);
  and and_3 (y2, not_1_out, X1, not_3_out, E);
  and and_4 (y3, not_1_out, X1, X2, E);
  and and_5 (y4, X0, not_2_out, not_3_out, E);
  and and_6 (y5, X0, not_2_out, X2, E);
  and and_7 (y6, X0, X1, not_3_out, E);
  and and_8 (y7, X0, X1, X2, E);

  // Notes on the sheet:
  //   A'B'C'
  //   A'B'C
  //   A'BC'
  //   A'BC
  //   AB'C'
  //   AB'C
  //   ABC'
  //   ABC
endmodule

// Dcdr 2->4
module Decoder_2__4 (
  input  X1,
  input  X0,
  output y0,
  output y1,
  output y2,
  output y3
);

  wire not_1_out, not_2_out;

  not not_1 (not_1_out, X1);
  not not_2 (not_2_out, X0);
  nor nor_1 (y0, X0, X1);
  nor nor_2 (y1, X0, not_1_out);
  nor nor_3 (y2, not_2_out, X1);
  nor nor_4 (y3, not_2_out, not_1_out);

  // Notes on the sheet:
  //   A'B'
  //   A'B
  //   AB'
  //   AB
endmodule

// MUX 2->1
module Multiplexer_2__1 (
  input  S,
  input  I0,
  input  I1,
  output O
);

  wire and_1_out, and_2_out, not_1_out;

  not not_1 (not_1_out, S);
  and and_1 (and_1_out, I0, not_1_out);
  or or_1 (O, and_1_out, and_2_out);
  and and_2 (and_2_out, I1, S);
endmodule

// MUX 4->1
module Multiplexer_4__1 (
  input  I0,
  input  I1,
  input  I2,
  input  I3,
  input  S0,
  input  S1,
  output O
);

  wire and_1_out, and_2_out, and_3_out, and_4_out, decoder_2_4_1_y0, decoder_2_4_1_y1, decoder_2_4_1_y2,
       decoder_2_4_1_y3;

  Decoder_2__4 decoder_2_4_1 (
    .X0(S0), .y0(decoder_2_4_1_y0), .y1(decoder_2_4_1_y1), .y2(decoder_2_4_1_y2), .y3(decoder_2_4_1_y3),
    .X1(S1));
  and and_1 (and_1_out, decoder_2_4_1_y0, I0);
  and and_2 (and_2_out, decoder_2_4_1_y1, I1);
  and and_3 (and_3_out, I2, decoder_2_4_1_y2);
  and and_4 (and_4_out, I3, decoder_2_4_1_y3);
  or or_1 (O, and_1_out, and_2_out, and_3_out, and_4_out);
endmodule

// Mlt.4x4
module Multiplier_4x4_bit (
  input  A0,
  input  A1,
  input  A2,
  input  A3,
  input  B3,
  input  B2,
  input  B1,
  input  B0,
  output P0,
  output P1,
  output P2,
  output P3,
  output P4,
  output P5,
  output P6,
  output P7
);

  wire full_adder_4bit_1_co, half_adder_1bit_1_co, multiplier_2x4_bit_1_c2, multiplier_2x4_bit_1_c3,
       multiplier_2x4_bit_1_c4, multiplier_2x4_bit_1_c5, multiplier_2x4_bit_2_c0, multiplier_2x4_bit_2_c1,
       multiplier_2x4_bit_2_c2, multiplier_2x4_bit_2_c3, multiplier_2x4_bit_2_c4, multiplier_2x4_bit_2_c5;

  Multiplier_2x4_bit multiplier_2x4_bit_1 (
    .A0(B0), .B0(A0), .B1(A1), .B2(A2), .B3(A3), .A1(B1), .C0(P0), .C1(P1), .C2(multiplier_2x4_bit_1_c2),
    .C3(multiplier_2x4_bit_1_c3), .C4(multiplier_2x4_bit_1_c4), .C5(multiplier_2x4_bit_1_c5));
  Multiplier_2x4_bit multiplier_2x4_bit_2 (
    .A0(B2), .B0(A0), .B1(A1), .B2(A2), .B3(A3), .A1(B3), .C0(multiplier_2x4_bit_2_c0),
    .C1(multiplier_2x4_bit_2_c1), .C2(multiplier_2x4_bit_2_c2), .C3(multiplier_2x4_bit_2_c3),
    .C4(multiplier_2x4_bit_2_c4), .C5(multiplier_2x4_bit_2_c5));
  Full_Adder_4bit full_adder_4bit_1 (
    .Ci(1'b0), .A3(multiplier_2x4_bit_1_c2), .A2(multiplier_2x4_bit_1_c3), .A1(multiplier_2x4_bit_1_c4),
    .A0(multiplier_2x4_bit_1_c5), .Co(full_adder_4bit_1_co), .S3(P5), .B3(multiplier_2x4_bit_2_c0), .S2(P4),
    .B2(multiplier_2x4_bit_2_c1), .S1(P3), .B1(multiplier_2x4_bit_2_c2), .S0(P2), .B0(multiplier_2x4_bit_2_c3));
  Half_Adder_1bit half_adder_1bit_1 (
    .A(full_adder_4bit_1_co), .B(multiplier_2x4_bit_2_c4), .S(P6), .Co(half_adder_1bit_1_co));
  Half_Adder_1bit half_adder_1bit_2 (.A(half_adder_1bit_1_co), .B(multiplier_2x4_bit_2_c5), .S(P7));  // open: Co
endmodule

// Cmp.4
module Comperator_4bit (
  input  A0,
  input  A1,
  input  A2,
  input  A3,
  input  B0,
  input  B1,
  input  B2,
  input  B3,
  output A_B,
  output A_B_2,
  output A_B_3
);

  wire and_1_out, and_3_out, comperator_2bit_1_a_b, comperator_2bit_1_a_b_2, comperator_2bit_1_a_b_3,
       comperator_2bit_2_a_b, comperator_2bit_2_a_b_2, comperator_2bit_2_a_b_3;

  Comperator_2bit comperator_2bit_1 (
    .A1(A1), .B1(B1), .A0(A0), .B0(B0), .A_B(comperator_2bit_1_a_b), .A_B_2(comperator_2bit_1_a_b_2),
    .A_B_3(comperator_2bit_1_a_b_3));
  Comperator_2bit comperator_2bit_2 (
    .A1(A3), .B1(B3), .A0(A2), .B0(B2), .A_B(comperator_2bit_2_a_b), .A_B_2(comperator_2bit_2_a_b_2),
    .A_B_3(comperator_2bit_2_a_b_3));
  or or_1 (A_B, comperator_2bit_1_a_b, and_1_out);
  and and_1 (and_1_out, comperator_2bit_1_a_b_2, comperator_2bit_2_a_b);
  and and_2 (A_B_2, comperator_2bit_1_a_b_2, comperator_2bit_2_a_b_2);
  or or_2 (A_B_3, comperator_2bit_1_a_b_3, and_3_out);
  and and_3 (and_3_out, comperator_2bit_1_a_b_2, comperator_2bit_2_a_b_3);
endmodule

// MUX 2->1 .8
module Multiplexer_2__1_8bit (
  input  S,
  input  E,
  input  A0,
  input  B0,
  input  A1,
  input  B1,
  input  A2,
  input  B2,
  input  A3,
  input  B3,
  input  A4,
  input  B4,
  input  A5,
  input  B5,
  input  A6,
  input  B6,
  input  A7,
  input  B7,
  output O0,
  output O1,
  output O2,
  output O3,
  output O4,
  output O5,
  output O6,
  output _7O
);

  wire and_1_out, and_2_out, and_3_out, and_4_out, and_5_out, and_6_out, and_7_out, and_8_out, and_9_out,
       and_10_out, and_11_out, and_12_out, and_13_out, and_14_out, and_15_out, and_16_out, not_1_out,
       not_2_out, not_3_out, not_4_out, not_5_out, not_6_out, not_7_out, not_8_out, not_9_out;

  not not_1 (not_1_out, E);
  not not_2 (not_2_out, S);
  not not_3 (not_3_out, S);
  not not_4 (not_4_out, S);
  not not_5 (not_5_out, S);
  not not_6 (not_6_out, S);
  not not_7 (not_7_out, S);
  not not_8 (not_8_out, S);
  not not_9 (not_9_out, S);
  and and_1 (and_1_out, A0, not_1_out, not_2_out);
  or or_1 (O0, and_1_out, and_2_out);
  and and_2 (and_2_out, B0, not_1_out, S);
  and and_3 (and_3_out, A1, not_1_out, not_3_out);
  or or_2 (O1, and_3_out, and_4_out);
  and and_4 (and_4_out, B1, not_1_out, S);
  and and_5 (and_5_out, A2, not_1_out, not_4_out);
  or or_3 (O2, and_5_out, and_6_out);
  and and_6 (and_6_out, B2, not_1_out, S);
  and and_7 (and_7_out, A3, not_1_out, not_5_out);
  or or_4 (O3, and_7_out, and_8_out);
  and and_8 (and_8_out, B3, not_1_out, S);
  and and_9 (and_9_out, A4, not_1_out, not_6_out);
  or or_5 (O4, and_9_out, and_10_out);
  and and_10 (and_10_out, B4, not_1_out, S);
  and and_11 (and_11_out, A5, not_1_out, not_7_out);
  or or_6 (O5, and_11_out, and_12_out);
  and and_12 (and_12_out, B5, not_1_out, S);
  and and_13 (and_13_out, A6, not_1_out, not_8_out);
  or or_7 (O6, and_13_out, and_14_out);
  and and_14 (and_14_out, B6, not_1_out, S);
  and and_15 (and_15_out, A7, not_1_out, not_9_out);
  or or_8 (_7O, and_15_out, and_16_out);
  and and_16 (and_16_out, B7, not_1_out, S);
endmodule

// Dcdr 4->16
module Decoder_4__16 (
  input  x0,
  input  x1,
  input  x2,
  input  x3,
  output y0,
  output y1,
  output y2,
  output y8,
  output y3,
  output y9,
  output y4,
  output y10,
  output y5,
  output y11,
  output y6,
  output y12,
  output y7,
  output y13,
  output y14,
  output y15
);

  wire not_1_out;

  not not_1 (not_1_out, x0);
  Decoder_3__8 decoder_3_8_1 (
    .X0(x1), .X1(x2), .X2(x3), .y0(y0), .y1(y1), .y2(y2), .y3(y3), .y4(y4), .y5(y5), .y6(y6), .y7(y7),
    .E(not_1_out));
  Decoder_3__8 decoder_3_8_2 (
    .X0(x1), .X1(x2), .X2(x3), .y0(y8), .y1(y9), .y2(y10), .y3(y11), .y4(y12), .y5(y13), .y6(y14), .y7(y15),
    .E(x0));

  // Notes on the sheet:
  //   AB'C'D'
  //   AB'C'D
  //   AB'CD'
  //   AB'CD
  //   ABC'D'
  //   ABC'D
  //   ABCD'
  //   ABCD
  //   A'B'C'D'
  //   A'B'C'D
  //   A'B'CD'
  //   A'B'CD
  //   A'BC'D'
  //   A'BC'D
  //   A'BCD'
  //   A'BCD
endmodule
