// Logisim project Sequential.circ as structural Verilog: 18 circuits, main circuit main
module main (
);

  Synchronous_Counter__4bit synchronous_counter_4bit_1 ();  // open: En, Cle, Clk, Q0, Q1, Q2, Q3
endmodule

// SR-L
module SR_Latch (
  input  Cle,
  input  R,
  input  S,
  input  Pre,
  output out_5,
  output out_6
);

  nor nor_1 (out_5, R, Cle, out_6);
  nor nor_2 (out_6, out_5, Pre, S);
endmodule

// SR-FF
module SR_Flip_Flop (
  input  Clk,
  input  Pre,
  input  S,
  input  R,
  input  Cle,
  output Q,
  output Q_prime
);

  wire and_1_out, and_2_out;

  and and_1 (and_1_out, S, Clk);
  and and_2 (and_2_out, Clk, R);
  SR_Latch sr_latch_1 (.Pre(Pre), .R(and_2_out), .S(and_1_out), .Cle(Cle), .out_5(Q), .out_6(Q_prime));
endmodule

// D-FF
module D_Flip_Flop (
  input  Pre,
  input  Clk,
  input  D,
  input  Cle,
  output Q,
  output Q_prime
);

  wire not_1_out;

  not not_1 (not_1_out, D);
  SR_Flip_Flop sr_flip_flop_1 (.S(D), .R(not_1_out), .Q(Q), .Q_prime(Q_prime), .Clk(Clk), .Pre(Pre), .Cle(Cle));
endmodule

// D-FF v.2
module D_Flip_Flop_version_2__MS (
  input  Pre,
  input  D,
  input  Cle,
  input  Clk,
  output Q,
  output Q_prime
);

  wire d_flip_flop_1_q, not_1_out;

  D_Flip_Flop d_flip_flop_1 (.D(D), .Q(d_flip_flop_1_q), .Clk(Clk), .Pre(Pre), .Cle(Cle));  // open: Q_prime
  not not_1 (not_1_out, Clk);
  D_Flip_Flop d_flip_flop_2 (.D(d_flip_flop_1_q), .Q(Q), .Q_prime(Q_prime), .Clk(not_1_out), .Pre(Pre), .Cle(Cle));
endmodule

// JK-FF v.1
module JK_Flip_Flop_version_1 (
  input  Clk,
  input  Pre,
  input  K,
  input  J,
  input  Cle,
  output Q,
  output Q_prime
);

  wire and_1_out, and_2_out, not_1_out, or_1_out;

  not not_1 (not_1_out, K);
  and and_1 (and_1_out, not_1_out, Q);
  or or_1 (or_1_out, and_1_out, and_2_out);
  and and_2 (and_2_out, Q_prime, J);
  D_Flip_Flop_version_2__MS d_flip_flop_version_2_ms_1 (
    .Pre(Pre), .D(or_1_out), .Cle(Cle), .Clk(Clk), .Q(Q), .Q_prime(Q_prime));
endmodule

// JK-FF v.2
module JK_Flip_Flop_version_2__MS (
  input  Clk,
  input  Pre,
  input  J,
  input  K,
  input  Cle,
  output Q,
  output Q_prime
);

  wire and_1_out, and_2_out, and_3_out, and_4_out, not_1_out, sr_latch_1_out_5, sr_latch_1_out_6;

  and and_1 (and_1_out, Q_prime, J, Clk);
  SR_Latch sr_latch_1 (
    .Pre(Pre), .R(and_2_out), .S(and_1_out), .Cle(Cle), .out_5(sr_latch_1_out_5), .out_6(sr_latch_1_out_6));
  and and_2 (and_2_out, Clk, K, Q);
  not not_1 (not_1_out, Clk);
  and and_3 (and_3_out, sr_latch_1_out_5, not_1_out);
  and and_4 (and_4_out, not_1_out, sr_latch_1_out_6);
  SR_Latch sr_latch_2 (.Pre(Pre), .R(and_4_out), .S(and_3_out), .Cle(Cle), .out_5(Q), .out_6(Q_prime));
endmodule

// T-FF
module T_Flip_Flop (
  input  Clk,
  input  Pre,
  input  T,
  input  Cle,
  output Q,
  output Q_prime
);

  JK_Flip_Flop_version_2__MS jk_flip_flop_version_2_ms_1 (
    .Pre(Pre), .J(T), .K(T), .Cle(Cle), .Q(Q), .Q_prime(Q_prime), .Clk(Clk));
endmodule

// Sh.Reg.
module Shift_Register__D_FF (
  input  Pre,
  input  Ctrl,
  input  D,
  input  Cle,
  output Q
);

  wire and_1_out, d_flip_flop_version_2_ms_1_q, d_flip_flop_version_2_ms_2_q, d_flip_flop_version_2_ms_3_q;

  and and_1 (and_1_out, Ctrl, 1'b1);
  D_Flip_Flop_version_2__MS d_flip_flop_version_2_ms_1 (
    .Pre(Pre), .D(D), .Cle(Cle), .Clk(and_1_out), .Q(d_flip_flop_version_2_ms_1_q));  // open: Q_prime
  D_Flip_Flop_version_2__MS d_flip_flop_version_2_ms_2 (
    .Pre(Pre), .D(d_flip_flop_version_2_ms_3_q), .Cle(Cle), .Clk(and_1_out), .Q(d_flip_flop_version_2_ms_2_q));  // open: Q_prime
  D_Flip_Flop_version_2__MS d_flip_flop_version_2_ms_3 (
    .Pre(Pre), .D(d_flip_flop_version_2_ms_1_q), .Cle(Cle), .Clk(and_1_out), .Q(d_flip_flop_version_2_ms_3_q));  // open: Q_prime
  D_Flip_Flop_version_2__MS d_flip_flop_version_2_ms_4 (
    .Pre(Pre), .D(d_flip_flop_version_2_ms_2_q), .Cle(Cle), .Clk(and_1_out), .Q(Q));  // open: Q_prime
endmodule

module Sh_Reg__Adder (
  input  D1,
  input  in_2,
  input  D2,
  output out_4
);

  wire d_flip_flop_version_2_ms_1_q, full_adder_1bit_1_co, shift_register_d_ff_1_q, shift_register_d_ff_2_q;

  Shift_Register__D_FF shift_register_d_ff_1 (.Pre(1'b0), .Ctrl(in_2), .D(D1), .Cle(1'b0), .Q(shift_register_d_ff_1_q));
  D_Flip_Flop_version_2__MS d_flip_flop_version_2_ms_1 (
    .Pre(1'b0), .D(full_adder_1bit_1_co), .Cle(1'b0), .Clk(in_2), .Q(d_flip_flop_version_2_ms_1_q));  // open: Q_prime
  Shift_Register__D_FF shift_register_d_ff_2 (.Pre(1'b0), .Ctrl(in_2), .D(D2), .Cle(1'b0), .Q(shift_register_d_ff_2_q));
  Full_Adder_1bit full_adder_1bit_1 (
    .A(shift_register_d_ff_2_q), .B(shift_register_d_ff_1_q), .Ci(d_flip_flop_version_2_ms_1_q), .S(out_4),
    .Co(full_adder_1bit_1_co));
endmodule

module Shift_Register__pm_D_FF (
  input  Clk,
  input  D,
  input  Pre,
  input  Cle,
  output Q0,
  output Q1,
  output Q2,
  output Q3,
  output Q
);

  D_Flip_Flop_part d_ff_1 (.clk(Clk), .D(D), .Q(Q0), .preset(Pre), .en(1'b1), .reset(Cle));  // open: Qn
  D_Flip_Flop_part d_ff_2 (.clk(Clk), .D(Q1), .Q(Q2), .preset(Pre), .en(1'b1), .reset(Cle));  // open: Qn
  D_Flip_Flop_part d_ff_3 (.clk(Clk), .D(Q0), .Q(Q1), .preset(Pre), .en(1'b1), .reset(Cle));  // open: Qn
  D_Flip_Flop_part d_ff_4 (.clk(Clk), .D(Q2), .Q(Q), .preset(Pre), .en(1'b1), .reset(Cle));  // open: Qn

  assign Q3 = Q;
endmodule

module Shift_Register__JK_FF (
  input  Clk,
  input  Pre,
  input  D,
  input  Cle,
  output Q,
  output out_6,
  output out_7,
  output out_8,
  output out_9
);

  wire not_1_out, not_2_out, not_3_out, not_4_out;

  not not_1 (not_1_out, D);
  JK_Flip_Flop_version_1 jk_flip_flop_version_1_1 (
    .J(D), .K(not_1_out), .Q(out_6), .Clk(Clk), .Pre(Pre), .Cle(Cle));  // open: Q_prime
  not not_2 (not_2_out, out_6);
  JK_Flip_Flop_version_1 jk_flip_flop_version_1_2 (
    .J(out_6), .K(not_2_out), .Q(out_7), .Clk(Clk), .Pre(Pre), .Cle(Cle));  // open: Q_prime
  not not_3 (not_3_out, out_7);
  JK_Flip_Flop_version_1 jk_flip_flop_version_1_3 (
    .J(out_8), .K(not_4_out), .Q(out_9), .Clk(Clk), .Pre(Pre), .Cle(Cle));  // open: Q_prime
  JK_Flip_Flop_version_1 jk_flip_flop_version_1_4 (
    .J(out_7), .K(not_3_out), .Q(out_8), .Clk(Clk), .Pre(Pre), .Cle(Cle));  // open: Q_prime
  not not_4 (not_4_out, out_8);

  assign Q = out_9;
endmodule

// +
module Sh_Reg__Adder__JK (
  input  Pre,
  input  D1,
  input  Clk,
  input  D2,
  input  Cle,
  output Q
);

  wire full_adder_1bit_1_co, jk_flip_flop_version_1_1_q, not_1_out, shift_register_jk_ff_1_q,
       shift_register_jk_ff_2_q;

  JK_Flip_Flop_version_1 jk_flip_flop_version_1_1 (
    .J(full_adder_1bit_1_co), .K(not_1_out), .Q(jk_flip_flop_version_1_1_q), .Clk(Clk), .Pre(Pre), .Cle(Cle));  // open: Q_prime
  not not_1 (not_1_out, full_adder_1bit_1_co);
  Shift_Register__JK_FF shift_register_jk_ff_1 (
    .Clk(Clk), .Pre(Pre), .D(D1), .Cle(Cle), .Q(shift_register_jk_ff_1_q));  // open: out_6, out_7, out_8, out_9
  Shift_Register__JK_FF shift_register_jk_ff_2 (
    .Clk(Clk), .Pre(Pre), .D(D2), .Cle(Cle), .Q(shift_register_jk_ff_2_q));  // open: out_6, out_7, out_8, out_9
  Full_Adder_1bit full_adder_1bit_1 (
    .A(shift_register_jk_ff_2_q), .B(shift_register_jk_ff_1_q), .Ci(jk_flip_flop_version_1_1_q), .S(Q),
    .Co(full_adder_1bit_1_co));
endmodule

module Ripple_Counter__4bit (
  input  Clk,
  input  Cle,
  input  En,
  output Q0,
  output Q1,
  output Q2,
  output Q3
);

  wire not_5_out, t_ff_1_qn, t_ff_2_qn, t_ff_3_qn, t_ff_4_qn;

  not not_1 (Q3, t_ff_1_qn);
  T_Flip_Flop_part t_ff_1 (.clk(Clk), .T(En), .Qn(t_ff_1_qn), .preset(1'b0), .reset(Cle), .en(not_5_out));  // open: Q
  not not_2 (Q2, t_ff_2_qn);
  T_Flip_Flop_part t_ff_2 (
    .clk(t_ff_1_qn), .T(En), .Qn(t_ff_2_qn), .preset(1'b0), .reset(Cle), .en(not_5_out));  // open: Q
  T_Flip_Flop_part t_ff_3 (
    .clk(t_ff_2_qn), .T(En), .Qn(t_ff_3_qn), .preset(1'b0), .reset(Cle), .en(not_5_out));  // open: Q
  not not_3 (Q0, t_ff_4_qn);
  not not_4 (Q1, t_ff_3_qn);
  T_Flip_Flop_part t_ff_4 (
    .clk(t_ff_3_qn), .T(En), .Qn(t_ff_4_qn), .preset(1'b0), .reset(Cle), .en(not_5_out));  // open: Q
  not not_5 (not_5_out, 1'b0);
endmodule

module Synchronous_Counter__4bit (
  input  En,
  input  Cle,
  input  Clk,
  output Q0,
  output Q1,
  output Q2,
  output Q3
);

  wire and_1_out, and_2_out, not_1_out;

  J_K_Flip_Flop #(.trigger("falling")) j_k_ff_1 (
    .J(En), .clk(Clk), .K(En), .Qn(Q3), .preset(Cle), .en(not_1_out), .reset(1'b0));  // open: Q
  J_K_Flip_Flop #(.trigger("falling")) j_k_ff_2 (
    .J(Q3), .clk(Clk), .K(Q3), .Qn(Q2), .preset(Cle), .en(not_1_out), .reset(1'b0));  // open: Q
  and and_1 (and_1_out, Q3, Q2);
  J_K_Flip_Flop #(.trigger("falling")) j_k_ff_3 (
    .J(and_1_out), .clk(Clk), .K(and_1_out), .Qn(Q1), .preset(Cle), .en(not_1_out), .reset(1'b0));  // open: Q
  and and_2 (and_2_out, and_1_out, Q1);
  J_K_Flip_Flop #(.trigger("falling")) j_k_ff_4 (
    .J(and_2_out), .clk(Clk), .K(and_2_out), .Qn(Q0), .preset(Cle), .en(not_1_out), .reset(1'b0));  // open: Q
  not not_1 (not_1_out, 1'b0);
endmodule

module Bi__Counter__4bit (
  input  En,
  input  Dir,
  input  Cle,
  input  Clk,
  output out_5,
  output out_6,
  output out_7,
  output out_8
);

  wire and_1_out, and_2_out, and_3_out, and_4_out, and_5_out, and_6_out, j_k_ff_1_qn, j_k_ff_2_qn,
       j_k_ff_3_qn, not_1_out, or_1_out, or_2_out, or_3_out;

  J_K_Flip_Flop #(.trigger("falling")) j_k_ff_1 (
    .J(En), .clk(Clk), .K(En), .Q(out_8), .Qn(j_k_ff_1_qn), .preset(1'b0), .en(En), .reset(Cle));
  not not_1 (not_1_out, Dir);
  and and_1 (and_1_out, Dir, out_8);
  or or_1 (or_1_out, and_1_out, and_2_out);
  and and_2 (and_2_out, j_k_ff_1_qn, not_1_out);
  and and_3 (and_3_out, and_1_out, out_7);
  J_K_Flip_Flop #(.trigger("falling")) j_k_ff_2 (
    .J(or_1_out), .clk(Clk), .K(or_1_out), .Q(out_7), .Qn(j_k_ff_2_qn), .preset(1'b0), .en(En), .reset(Cle));
  and and_4 (and_4_out, j_k_ff_2_qn, and_2_out);
  or or_2 (or_2_out, and_3_out, and_4_out);
  and and_5 (and_5_out, and_3_out, out_6);
  J_K_Flip_Flop #(.trigger("falling")) j_k_ff_3 (
    .J(or_2_out), .clk(Clk), .K(or_2_out), .Q(out_6), .Qn(j_k_ff_3_qn), .preset(1'b0), .en(En), .reset(Cle));
  or or_3 (or_3_out, and_5_out, and_6_out);
  and and_6 (and_6_out, j_k_ff_3_qn, and_4_out);
  J_K_Flip_Flop #(.trigger("falling")) j_k_ff_4 (
    .J(or_3_out), .clk(Clk), .K(or_3_out), .Q(out_5), .preset(1'b0), .en(En), .reset(Cle));  // open: Qn
endmodule

module Ripple_Counter__5bit (
  input  Clk,
  input  Cle,
  input  En,
  output Q0,
  output Q1,
  output Q2,
  output Q3,
  output Q5
);

  wire not_1_out;

  J_K_Flip_Flop #(.trigger("falling")) j_k_ff_1 (
    .J(En), .clk(Clk), .K(En), .Qn(Q5), .preset(Cle), .en(not_1_out), .reset(1'b0));  // open: Q
  J_K_Flip_Flop #(.trigger("falling")) j_k_ff_2 (
    .J(En), .clk(Q3), .K(En), .Qn(Q2), .preset(Cle), .en(not_1_out), .reset(1'b0));  // open: Q
  J_K_Flip_Flop #(.trigger("falling")) j_k_ff_3 (
    .J(En), .clk(Q5), .K(En), .Qn(Q3), .preset(Cle), .en(not_1_out), .reset(1'b0));  // open: Q
  J_K_Flip_Flop #(.trigger("falling")) j_k_ff_4 (
    .J(En), .clk(Q2), .K(En), .Qn(Q1), .preset(Cle), .en(not_1_out), .reset(1'b0));  // open: Q
  J_K_Flip_Flop #(.trigger("falling")) j_k_ff_5 (
    .J(En), .clk(Q1), .K(En), .Qn(Q0), .preset(Cle), .en(not_1_out), .reset(1'b0));  // open: Q
  not not_1 (not_1_out, 1'b0);
endmodule

module Synchronous_Counter__5bit (
  input  Clk,
  input  En,
  input  Cle,
  output Q0,
  output Q1,
  output Q2,
  output Q3,
  output Q4
);

  wire and_1_out, and_2_out, and_3_out, and_4_out, and_5_out, and_6_out, and_7_out, and_8_out, and_9_out,
       and_10_out, and_11_out, and_12_out, and_13_out, d_ff_1_q, d_ff_2_q, d_ff_3_q, d_ff_4_q, d_ff_5_q,
       not_1_out, not_2_out, not_3_out, not_4_out, not_5_out, or_1_out, or_2_out, or_3_out, or_4_out,
       or_5_out;

  not not_1 (not_1_out, En);
  and and_1 (and_1_out, not_1_out, d_ff_1_q);
  and and_2 (and_2_out, Q4, En);
  D_Flip_Flop_part d_ff_1 (.clk(Clk), .D(or_1_out), .Q(d_ff_1_q), .Qn(Q4), .preset(Cle), .en(En), .reset(1'b0));
  or or_1 (or_1_out, and_1_out, and_2_out);
  not not_2 (not_2_out, Q4);
  and and_3 (and_3_out, not_2_out, d_ff_2_q);
  and and_4 (and_4_out, Q3, Q4);
  D_Flip_Flop_part d_ff_2 (.clk(Clk), .D(or_2_out), .Q(d_ff_2_q), .Qn(Q3), .preset(Cle), .en(En), .reset(1'b0));
  or or_2 (or_2_out, and_3_out, and_4_out);
  not not_3 (not_3_out, and_5_out);
  and and_5 (and_5_out, Q3, Q4);
  and and_6 (and_6_out, not_3_out, d_ff_3_q);
  and and_7 (and_7_out, Q2, and_5_out);
  D_Flip_Flop_part d_ff_3 (.clk(Clk), .D(or_3_out), .Q(d_ff_3_q), .Qn(Q2), .preset(Cle), .en(En), .reset(1'b0));
  or or_3 (or_3_out, and_6_out, and_7_out);
  not not_4 (not_4_out, and_8_out);
  and and_8 (and_8_out, Q2, and_5_out);
  and and_9 (and_9_out, not_4_out, d_ff_4_q);
  or or_4 (or_4_out, and_9_out, and_10_out);
  and and_10 (and_10_out, Q1, and_8_out);
  not not_5 (not_5_out, and_11_out);
  D_Flip_Flop_part d_ff_4 (.clk(Clk), .D(or_4_out), .Q(d_ff_4_q), .Qn(Q1), .preset(Cle), .en(En), .reset(1'b0));
  and and_11 (and_11_out, Q1, and_8_out);
  and and_12 (and_12_out, not_5_out, d_ff_5_q);
  or or_5 (or_5_out, and_12_out, and_13_out);
  and and_13 (and_13_out, Q0, and_11_out);
  D_Flip_Flop_part d_ff_5 (.clk(Clk), .D(or_5_out), .Q(d_ff_5_q), .Qn(Q0), .preset(Cle), .en(En), .reset(1'b0));
endmodule
