// Logisim project RAM.circ as structural Verilog
module Counter_DFF (
  input  Clk,
  input  En,
  input  Cle,
  output Q0,
  output Q1,
  output Q2,
  output Q3,
  output Q4
);

  wire and_1_out, and_2_out, and_3_out, and_4_out, and_5_out, and_6_out, and_7_out, and_8_out, and_9_out,
       and_10_out, and_11_out, and_12_out, and_13_out, d_ff_1_q, d_ff_2_q, d_ff_3_q, d_ff_4_q, d_ff_5_q,
       not_1_out, not_2_out, not_3_out, not_4_out, not_5_out, or_1_out, or_2_out, or_3_out, or_4_out,
       or_5_out;

  not not_1 (not_1_out, En);
  and and_1 (and_1_out, not_1_out, d_ff_1_q);
  and and_2 (and_2_out, Q4, En);
  D_Flip_Flop d_ff_1 (.clk(Clk), .D(or_1_out), .Q(d_ff_1_q), .Qn(Q4), .preset(Cle), .en(En), .reset(1'b0));
  or or_1 (or_1_out, and_1_out, and_2_out);
  not not_2 (not_2_out, Q4);
  and and_3 (and_3_out, not_2_out, d_ff_2_q);
  and and_4 (and_4_out, Q3, Q4);
  D_Flip_Flop d_ff_2 (.clk(Clk), .D(or_2_out), .Q(d_ff_2_q), .Qn(Q3), .preset(Cle), .en(En), .reset(1'b0));
  or or_2 (or_2_out, and_3_out, and_4_out);
  not not_3 (not_3_out, and_5_out);
  and and_5 (and_5_out, Q3, Q4);
  and and_6 (and_6_out, not_3_out, d_ff_3_q);
  and and_7 (and_7_out, Q2, and_5_out);
  D_Flip_Flop d_ff_3 (.clk(Clk), .D(or_3_out), .Q(d_ff_3_q), .Qn(Q2), .preset(Cle), .en(En), .reset(1'b0));
  or or_3 (or_3_out, and_6_out, and_7_out);
  not not_4 (not_4_out, and_8_out);
  and and_8 (and_8_out, Q2, and_5_out);
  and and_9 (and_9_out, not_4_out, d_ff_4_q);
  or or_4 (or_4_out, and_9_out, and_10_out);
  and and_10 (and_10_out, Q1, and_8_out);
  not not_5 (not_5_out, and_11_out);
  D_Flip_Flop d_ff_4 (.clk(Clk), .D(or_4_out), .Q(d_ff_4_q), .Qn(Q1), .preset(Cle), .en(En), .reset(1'b0));
  and and_11 (and_11_out, Q1, and_8_out);
  and and_12 (and_12_out, not_5_out, d_ff_5_q);
  or or_5 (or_5_out, and_12_out, and_13_out);
  and and_13 (and_13_out, Q0, and_11_out);
  D_Flip_Flop d_ff_5 (.clk(Clk), .D(or_5_out), .Q(d_ff_5_q), .Qn(Q0), .preset(Cle), .en(En), .reset(1'b0));
endmodule

module Counter_JKFF (
  input  Clk,
  input  Cle,
  input  En,
  output Q0,
  output Q1,
  output Q2,
  output Q3,
  output Q5
);

  wire j_k_ff_1_qn, j_k_ff_2_qn, j_k_ff_3_qn, j_k_ff_4_qn, not_1_out;

  J_K_Flip_Flop #(.trigger("falling")) j_k_ff_1 (
    .J(En), .clk(Clk), .K(En), .Q(Q5), .Qn(j_k_ff_1_qn), .preset(1'b0), .en(not_1_out), .reset(Cle));
  J_K_Flip_Flop #(.trigger("falling")) j_k_ff_2 (
    .J(En), .clk(j_k_ff_3_qn), .K(En), .Q(Q2), .Qn(j_k_ff_2_qn), .preset(1'b0), .en(not_1_out), .reset(Cle));
  J_K_Flip_Flop #(.trigger("falling")) j_k_ff_3 (
    .J(En), .clk(j_k_ff_1_qn), .K(En), .Q(Q3), .Qn(j_k_ff_3_qn), .preset(1'b0), .en(not_1_out), .reset(Cle));
  J_K_Flip_Flop #(.trigger("falling")) j_k_ff_4 (
    .J(En), .clk(j_k_ff_2_qn), .K(En), .Q(Q1), .Qn(j_k_ff_4_qn), .preset(1'b0), .en(not_1_out), .reset(Cle));
  J_K_Flip_Flop #(.trigger("falling")) j_k_ff_5 (
    .J(En), .clk(j_k_ff_4_qn), .K(En), .Q(Q0), .preset(1'b0), .en(not_1_out), .reset(Cle));  // open: Qn
  not not_1 (not_1_out, 1'b0);
endmodule

module RAM (
  input  On,
  input  Reset,
  input  and_Clear,
  input  Mode,
  output Q4,
  output Q3,
  output Q2,
  output Q1,
  output Q0
);

  wire and_1_out, clock_1_out, not_1_out;
  wire [4:0] counter_dff_1_q4, counter_jkff_1_q5;

  Clock clock_1 (.out(clock_1_out));
  Counter_DFF counter_dff_1 (
    .Clk(clock_1_out), .En(On), .Cle(Reset), .Q0(counter_dff_1_q4[4]), .Q1(counter_dff_1_q4[3]),
    .Q2(counter_dff_1_q4[2]), .Q3(counter_dff_1_q4[1]), .Q4(counter_dff_1_q4[0]));
  Counter_JKFF counter_jkff_1 (
    .Clk(clock_1_out), .Cle(Reset), .En(On), .Q0(counter_jkff_1_q5[4]), .Q1(counter_jkff_1_q5[3]),
    .Q2(counter_jkff_1_q5[2]), .Q3(counter_jkff_1_q5[1]), .Q5(counter_jkff_1_q5[0]));
  and and_1 (and_1_out, Reset, and_Clear);
  RAM_part #(.addrWidth(5), .dataWidth(5), .bus("separate")) ram_1 (
    .addr(counter_dff_1_q4), .din(counter_jkff_1_q5), .data({Q4, Q3, Q2, Q1, Q0}), .str(Mode),
    .clk(clock_1_out), .ld(not_1_out), .clr(and_1_out));  // open: sel
  not not_1 (not_1_out, Mode);
  Hex_Digit_Display hex_digit_display_1 (.value({Q3, Q2, Q1, Q0}));  // open: dp
  Hex_Digit_Display hex_digit_display_2 (.value({3'b000, Q4}));  // open: dp

  // Notes on the sheet:
  //   1:Fill
  //   0:Test
endmodule
