// Logisim project ALU.circ as structural Verilog
// ALU(base)
module ALU_basic (
  input  [1:0] A,
  input  Cin,
  input  [1:0] B,
  input  [2:0] F,
  output [1:0] Out
);

  wire [1:0] adder_1_out, adder_2_out, nand_1_out, not_1_out, xor_1_out;

  assign not_1_out = ~A;  // NOT_Gate not_1, 2 bits wide
  Adder #(.width(2)) adder_1 (.a(A), .b(B), .out(adder_1_out), .cin(Cin));  // open: cout
  assign xor_1_out = A ^ B;  // XOR_Gate xor_1, 2 bits wide
  assign nand_1_out = ~(A & B);  // NAND_Gate nand_1, 2 bits wide
  Adder #(.width(2)) adder_2 (.a(A), .b(2'b00), .out(adder_2_out), .cin(1'b1));  // open: cout
  Multiplexer #(.select(3), .width(2), .enable("false")) multiplexer_1 (
    .in0(not_1_out), .in1(adder_1_out), .in2(xor_1_out), .in3(nand_1_out), .in4(adder_2_out), .in5(2'b00),
    .in6(2'b00), .in7(2'b00), .out(Out), .sel(F));

  // Notes on the sheet:
  //   Ā
  //   A+B
  //   A⨁B
  //   ___
  //   A•B
  //   A+1
  //   000:
  //   Ā
  //   001:
  //   A+B
  //   010:
  //   A⨁B
  //   ___
  //   A•B
  //   011:
  //   A+1
  //   100:
  //   N/A (00)
  //   101:
  //   N/A (00)
  //   110:
  //   111:
  //   N/A (00)
endmodule

// ALU(alt)
module ALU__alternative (
  input  [1:0] A,
  input  Cin,
  input  [1:0] B,
  input  [2:0] F,
  output [1:0] Out,
  output Co
);

  wire adder_1_cout, adder_2_cout, and_1_out, and_2_out, not_2_out, not_3_out, not_4_out, not_5_out;
  wire [1:0] adder_1_out, adder_2_out, nand_1_out, not_1_out, xor_1_out;

  assign not_1_out = ~A;  // NOT_Gate not_1, 2 bits wide
  Adder #(.width(2)) adder_1 (.a(A), .b(B), .out(adder_1_out), .cin(Cin), .cout(adder_1_cout));
  assign xor_1_out = A ^ B;  // XOR_Gate xor_1, 2 bits wide
  assign nand_1_out = ~(A & B);  // NAND_Gate nand_1, 2 bits wide
  Adder #(.width(2)) adder_2 (.a(A), .b(2'b00), .out(adder_2_out), .cin(1'b1), .cout(adder_2_cout));
  Multiplexer #(.select(3), .width(2), .enable("false")) multiplexer_1 (
    .in0(not_1_out), .in1(adder_1_out), .in2(xor_1_out), .in3(nand_1_out), .in4(adder_2_out), .in5(2'b00),
    .in6(2'b00), .in7(2'b00), .out(Out), .sel(F));
  not not_2 (not_2_out, F[1]);
  not not_3 (not_3_out, F[2]);
  not not_4 (not_4_out, F[0]);
  not not_5 (not_5_out, F[1]);
  and and_1 (and_1_out, F[0], not_2_out, not_3_out, adder_1_cout);
  and and_2 (and_2_out, not_4_out, not_5_out, F[2], adder_2_cout);
  or or_1 (Co, and_1_out, and_2_out);

  // Notes on the sheet:
  //   Ā
  //   A+B
  //   A⨁B
  //   ___
  //   A•B
  //   A+1
  //   Ā
  //   000:
  //   001:
  //   A+B
  //   010:
  //   A⨁B
  //   ___
  //   011:
  //   A•B
  //   100:
  //   A+1
  //   101:
  //   N/A (00)
  //   N/A (00)
  //   110:
  //   111:
  //   N/A (00)
endmodule

// ALU
module ALU_conventional (
  input  A0,
  input  A1,
  input  Cin,
  input  B0,
  input  B1,
  input  F2,
  input  F1,
  input  F0,
  output Out0,
  output Out1
);

  ALU_basic alu_basic_1 (.A({A1, A0}), .Cin(Cin), .B({B1, B0}), .Out({Out1, Out0}), .F({F2, F1, F0}));
endmodule
