// Logisim project Counter.circ as structural Verilog
module Counter_0_8__basic (
  input  Clk,
  input  On,
  input  Clear,
  output [3:0] out_4
);

  wire and_1_out, and_2_out, and_3_out, not_1_out, not_2_out, or_1_out;

  or or_1 (or_1_out, Clear, and_3_out);
  J_K_Flip_Flop #(.trigger("falling")) j_k_ff_1 (
    .J(On), .clk(Clk), .K(On), .Q(out_4[0]), .en(On), .reset(or_1_out));  // open: Qn, preset
  J_K_Flip_Flop #(.trigger("falling")) j_k_ff_2 (
    .J(out_4[0]), .clk(Clk), .K(out_4[0]), .Q(out_4[1]), .en(On), .reset(or_1_out));  // open: Qn, preset
  and and_1 (and_1_out, out_4[1], out_4[0]);
  J_K_Flip_Flop #(.trigger("falling")) j_k_ff_3 (
    .J(and_1_out), .clk(Clk), .K(and_1_out), .Q(out_4[2]), .en(On), .reset(or_1_out));  // open: Qn, preset
  and and_2 (and_2_out, out_4[2], and_1_out);
  J_K_Flip_Flop #(.trigger("falling")) j_k_ff_4 (
    .J(and_2_out), .clk(Clk), .K(and_2_out), .Q(out_4[3]), .en(On), .reset(or_1_out));  // open: Qn, preset
  Hex_Digit_Display hex_digit_display_1 (.value(out_4));  // open: dp
  not not_1 (not_1_out, out_4[1]);
  and and_3 (and_3_out, out_4[0], not_1_out, not_2_out, out_4[3]);
  not not_2 (not_2_out, out_4[2]);
endmodule

module Counter_0_8__conventional (
  input  On,
  input  Clk,
  input  Clear,
  output Q3,
  output Q2,
  output Q1,
  output Q0
);

  Counter_0_8__basic counter_0_8_basic_1 (.Clk(Clk), .On(On), .Clear(Clear), .out_4({Q3, Q2, Q1, Q0}));
  Hex_Digit_Display hex_digit_display_1 (.value({Q3, Q2, Q1, Q0}));  // open: dp
endmodule
